// Logisim project Cpu.circ as structural Verilog
module main (
  input  [15:0] in_1,
  input  [15:0] in_2,
  input  [4:0] in_3,
  output [15:0] out_4,
  output JMP
);

  wire clk_out, undriven, undriven_2, undriven_3, undriven_4, undriven_5, undriven_6, undriven_7, undriven_8,
       undriven_9, undriven_10, undriven_11, undriven_12;
  wire [15:0] adder_1_out, and_1_out, divider_1_out, multiplier_1_out, not_1_out, or_1_out, or_2_out,
       shifter_1_out, shifter_2_out, subtractor_1_out;

  Clock clk (.out(clk_out));
  // RGB_Video #(.height(192), .scale(3), .width(256)) rgb_video_1: pin names not known
  registerwithreadenable r0 (
    .data_reg(out_4), .write_enable_reg(undriven), .clock_reg(clk_out), .read_enable_reg(undriven_12),
    .output_reg(out_4));
  registerwithreadenable r1 (
    .data_reg(out_4), .write_enable_reg(undriven_2), .clock_reg(clk_out), .output_reg(out_4));  // open: read_enable_reg
  registerwithreadenable r2 (
    .data_reg(out_4), .write_enable_reg(undriven_3), .clock_reg(clk_out), .output_reg(out_4));  // open: read_enable_reg
  registerwithreadenable r3 (
    .data_reg(out_4), .write_enable_reg(undriven_4), .clock_reg(clk_out), .output_reg(out_4));  // open: read_enable_reg
  registerwithreadenable r4 (
    .data_reg(out_4), .write_enable_reg(undriven_5), .clock_reg(clk_out), .output_reg(out_4));  // open: read_enable_reg
  registerwithreadenable r5 (
    .data_reg(out_4), .write_enable_reg(undriven_6), .clock_reg(clk_out), .output_reg(out_4));  // open: read_enable_reg
  registerwithreadenable r6 (
    .data_reg(out_4), .write_enable_reg(undriven_7), .clock_reg(clk_out), .output_reg(out_4));  // open: read_enable_reg
  registerwithreadenable r7 (
    .data_reg(out_4), .write_enable_reg(undriven_8), .clock_reg(clk_out), .output_reg(out_4));  // open: read_enable_reg
  registerwithreadenable r8 (
    .data_reg(out_4), .write_enable_reg(undriven_9), .clock_reg(clk_out), .output_reg(out_4));  // open: read_enable_reg
  registerwithreadenable r9 (
    .data_reg(out_4), .write_enable_reg(undriven_10), .clock_reg(clk_out), .output_reg(out_4));  // open: read_enable_reg
  registerwithreadenable r10 (
    .data_reg(out_4), .write_enable_reg(undriven_11), .clock_reg(clk_out), .output_reg(out_4));  // open: read_enable_reg
  registerwithreadenable r11 (
    .data_reg(out_4), .clock_reg(clk_out), .output_reg(out_4));  // open: write_enable_reg, read_enable_reg
  Pull_Resistor pull_resistor_1 (.node(out_4));
  Register #(.width(1)) JZ (.clk(clk_out));  // open: D, en, Q, clr
  ROM #(.addrWidth(16), .dataWidth(16)) Program_memory ();  // open: addr, data
  registerwithreadenable Jump_target_reg_r12 (
    .data_reg(out_4), .clock_reg(clk_out));  // open: write_enable_reg, read_enable_reg, output_reg
  Register #(.width(1)) JG ();  // open: D, en, clk, Q, clr
  registerwithreadenable accumulator_r13 ();  // open: data_reg, write_enable_reg, clock_reg, read_enable_reg, output_reg
  registerwithreadenable stack_ptr_r14 (
    .data_reg(out_4), .clock_reg(clk_out));  // open: write_enable_reg, read_enable_reg, output_reg
  registerwithreadenable memory_address_register_r15 (
    .data_reg(out_4), .clock_reg(clk_out));  // open: write_enable_reg, read_enable_reg, output_reg
  Register #(.width(1)) JS ();  // open: D, en, clk, Q, clr
  Register #(.width(1)) JO ();  // open: D, en, clk, Q, clr
  Register #(.width(1)) JV ();  // open: D, en, clk, Q, clr
  // DualRAM #(.addrWidth(16), .dataWidth(16)) data_memory: pin names not known
  Adder #(.width(16)) adder_1 (.out(adder_1_out));  // open: a, b, cin, cout
  Subtractor #(.width(16)) subtractor_1 (.out(subtractor_1_out));  // open: a, b, bin, bout
  Multiplier #(.mode("twosComplement"), .width(16)) multiplier_1 (.out(multiplier_1_out));  // open: a, b, cin, cout
  Divider #(.mode("twosComplement"), .width(16)) divider_1 (.out(divider_1_out));  // open: a, b, upper, rem
  // AND_Gate and_1 has open pins: out=and_1_out
  // OR_Gate or_1 has open pins: out=or_1_out
  // OR_Gate or_2 has open pins: out=or_2_out
  // NOT_Gate not_1 has open pins: in=open, out=not_1_out
  Shifter #(.width(16)) shifter_1 (.out(shifter_1_out));  // open: in, dist
  Shifter #(.shift("lr"), .width(16)) shifter_2 (.out(shifter_2_out));  // open: in, dist
  Comparator comparator_1 ();  // open: a, b, gt, eq, lt
  Multiplexer #(.select(5), .width(16)) multiplexer_1 (
    .in1(adder_1_out), .in2(subtractor_1_out), .in3(multiplier_1_out), .in4(divider_1_out), .in5(and_1_out),
    .in6(or_1_out), .in7(or_2_out), .in8(not_1_out), .in9(shifter_1_out), .in10(shifter_2_out), .sel(in_3));  // open: in0, in11, in12, in13, in14, in15, in16, in17, in18, in19, in20, in21, in22, in23, in24, in25, in26, in27, in28, in29, in30, in31, out

  assign JMP = 1'b1;
endmodule

module registerwithreadenable (
  input  [15:0] data_reg,
  input  write_enable_reg,
  input  clock_reg,
  input  read_enable_reg,
  output [15:0] output_reg
);

  wire [15:0] register_1_q;

  Register #(.width(16)) register_1 (
    .D(data_reg), .en(write_enable_reg), .clk(clock_reg), .Q(register_1_q));  // open: clr
  Multiplexer #(.width(16)) multiplexer_1 (.in1(register_1_q), .out(output_reg), .sel(read_enable_reg));  // open: in0
endmodule
